# Fritzing sketch Zoltar_init (saved by Fritzing 0.9.3b)
breadboards: 2

parts:
  Part1 = Arduino Mega 2560 (Rev3)
  R2 = Resistor [tolerance=±5% resistance=180 package="0603 [SMD]"]
  LED1 = LED - 3mm [color="Red (633nm)" package="3 mm [THT]"]
  R3 = Resistor [tolerance=±5% resistance=180 package="0603 [SMD]"]
  LED2 = LED - 3mm [color="Red (660nm)" package="3 mm [THT]"]
  LED3 = LED - 3mm [color="Red (660nm)" package="3 mm [THT]"]
  R4 = Resistor [tolerance=±5% resistance=180 package="0603 [SMD]"]
  LED4 = LED - 3mm [color="Yellow (595nm)" package="3 mm [THT]"]
  DFRobot_DFPlayer_Mini2 = DFRobot DFPlayer Mini [part_number=DFR0299]
  R5 = Resistor [tolerance=±5% resistance=1k package="0603 [SMD]"]
  SP1 = SPEAKER [package=pcb_mount_speaker]
  DFRobot_DFPlayer_Mini3 = DFRobot DFPlayer Mini [part_number=DFR0299]
  R6 = Resistor [tolerance=±5% resistance=1k package="0603 [SMD]"]
  R7 = Resistor [tolerance=±5% resistance=10k package="0603 [SMD]"]
  SP2 = SPEAKER [package=pcb_mount_speaker]
  R8 = Resistor [tolerance=±5% resistance=180 package="0603 [SMD]"]
  LED5 = LED - 3mm [color="Yellow (595nm)" package="3 mm [THT]"]
  S1 = Pushbutton [package="[THT]"]
  R9 = Resistor [tolerance=±5% resistance=1k package="0603 [SMD]"]
  D1 = Rectifier Diode [part_number=1N4001 package="300 mil [THT]"]
  Q1 = TIP120 Hi-Current Darlington Transistor
  R10 = Resistor [tolerance=±5% resistance=10k package="0603 [SMD]"]
  S2 = Pushbutton [package="[THT]"]
  R11 = Resistor [tolerance=±5% resistance=1k package="0603 [SMD]"]
  R12 = Resistor [tolerance=±5% resistance=1k package="0603 [SMD]"]

nets:
  N1: Part1.D13_PWM, R5.Pin_0
  N2: Part1.D12_PWM, DFRobot_DFPlayer_Mini2.TX
  N3: Part1.D11_PWM, R6.Pin_0
  N4: Part1.D2_PWM, R4.Pin_0
  N5: Part1.D3_PWM, R3.Pin_0
  N6: Part1.D4_PWM, R2.Pin_0
  N7: Part1.D5_PWM, R8.Pin_0
  N8: Part1.D7_PWM, R7.Pin_1, S1.Pin_1, S1.Pin_2
  N9: Part1.D31, R9.Pin_0
  N10: Part1.D33, R10.Pin_1, S2.Pin_3, S2.Pin_4
  N11: Part1.D35, R11.Pin_1
  N12: Part1.D37, R12.Pin_1
  N13: R2.Pin_1, LED1.anode
  N14: LED1.cathode, LED2.cathode, LED3.cathode, DFRobot_DFPlayer_Mini2.GND-1, DFRobot_DFPlayer_Mini2.GND-2, DFRobot_DFPlayer_Mini3.GND-1, DFRobot_DFPlayer_Mini3.GND-2, R7.Pin_0
  N15: R3.Pin_1, LED2.anode, LED3.anode
  N16: R4.Pin_1, LED4.anode
  N17: LED4.cathode, LED5.cathode
  VCC: DFRobot_DFPlayer_Mini2.VCC, DFRobot_DFPlayer_Mini3.VCC, S1.Pin_3, S1.Pin_4
  N18: DFRobot_DFPlayer_Mini2.RX, R5.Pin_1
  N19: DFRobot_DFPlayer_Mini2.SPK_1, SP1.-
  N20: DFRobot_DFPlayer_Mini2.SPK_2, SP1.+
  N21: DFRobot_DFPlayer_Mini3.RX, R6.Pin_1
  N22: DFRobot_DFPlayer_Mini3.SPK_1, SP2.-
  N23: DFRobot_DFPlayer_Mini3.SPK_2, SP2.+
  N24: R8.Pin_1, LED5.anode
  N25: R9.Pin_1, Q1.BASE
  N26: D1.cathode, R12.Pin_0
  N27: D1.anode, Q1.COLLECTOR
  N28: Q1.EMITTER, R11.Pin_0
  N29: S2.Pin_1, S2.Pin_2

notes:
  PIN 2: Backgruond Leds
  PIN 3: Eyes Leds
  PIN 4: Leds "Point to mouth
  PIN 5 : Leds "Push button coin"
  All this devices are working with 5 V
  PIN 31: Selenoid conexion to free coin if press button
  PIN 33: Button free coin
  PIN 35: Switch Win game sensor
  PIN 37: Switch Lost game sensor

// code stored in the sketch: Zoldar.ino
#include "Arduino.h"
#include "SoftwareSerial.h"
#include "DFRobotDFPlayerMini.h"
#include "Configuration.h"

DFRobotDFPlayerMini myDFPlayer;

int status;
boolean isStatusInit;
SoftwareSerial musicSoftwareSerial(MUSIC_RX_PIN, MUSIC_TX_PIN); // RX, TX

void setup() {
    isStatusInit = false;
    
    Serial.begin(9600);
    initMusicConfiguration();  
    
    status = STATUS_STAND_BY;
    pinMode(DETECT_COIN_PIN, INPUT);
} 

void loop() {

  //printStatus();

  switch (status) {

    case STATUS_INIT:
      statusInit();
      break;

    case STATUS_ACTIVATE_GAME:
      // Encender luces "Apunta a la boca"
      // Encender sonido campana
      // Activar los mandos
      //delay(10000);
      
      statusActivateGame();
      
      // Desactivar los mandos
      // Encender luces "Pulsa botón liberar moneda"
      // Activo siguiente estado WAITING_RELEASE_COIN

      break;

    case STATUS_WAITING_RELEASE_COIN:
      // Esperamos 10 segundos comprobando si se ha pulsado el botón de "liberar moneda"
      // Cuando se ha pulsado el botón o hayan pasado los 10 segundos, se libera la moneda.
      // Activo siguiente estado WIN_OR_LOST
      break;

    case STATUS_WIN_OR_LOST:
      // Chequeamos los sensores de acierto o no
      // Si ha acertado pasamos a "WIN" sino a "LOST"
      break;

    case STATUS_WIN:
        // Sacar tarjeta Acierto
        // Activar siguiente estado OFF
      break;

    case STATUS_LOST:
        // Sacar tarjeta de la tienda
        // Activar siguiente estado OFF
      break;

    case STATUS_OFF:
        // Esperar a que termine la música
        // desactivar musica y luces y movimiento. Todo
        // Activar siguiente estado STAND_BY
      break;

    default: //case "STAND_BY":
      statusStandBy();
      break;

  }
}


void initMusicConfiguration() {

  musicSoftwareSerial.begin(9600);
    if (!myDFPlayer.begin(musicSoftwareSerial)) {  //Use softwareSerial to communicate with mp3.
      while(true);
    }
    myDFPlayer.volume(MUSIC_VOLUME);
}

void playMusic() {
  myDFPlayer.play(1);  //Play the first mp3
}

// Input: Detectar moneda
void statusStandBy() {

  // Esperando a que llegue la señal de la moneda
  // Y cambio al siguiente estado INIT

  int inputCoin = digitalRead(DETECT_COIN_PIN);
  Serial.println(inputCoin);
  if (inputCoin == HIGH) {
    //status = STATUS_INIT;
  }
}

// Input: Play música
// Output: Led fondo
// Output: Led ojos
// Output: Mover boca
void statusInit() {
  Serial.println("statusInit");
  // Encender luces de fondo
  // Encender ojos
  // Encender movimiento de boca
  if (isStatusInit == false) {

    playMusic();
    backgroundLedOn();
    eyesLedOn();
    mouthMoveOn();
    
    isStatusInit = true;

    delay(DELAY_AFTER_STATUS_INIT);
  
    // cambiamos al siguiente estado ACTIVATE_GAME
    status = STATUS_ACTIVATE_GAME;
  }  
}

void statusActivateGame() {
  

}


void backgroundLedOn() {  
  
  
}

void eyesLedOn() {
  
  
}

void mouthMoveOn() {
  
  
}


void printStatus() {

  String statusText = "STAND_BY";

  switch (status) {
    
    case STATUS_INIT:
      statusText = "INIT";
    break;
    case STATUS_ACTIVATE_GAME:
      statusText = "ACTIVATE_GAME";
    break;
    case STATUS_WAITING_RELEASE_COIN:
      statusText = "WAITING_RELEASE_COIN";
    break;
    case STATUS_WIN_OR_LOST:
      statusText = "WIN_OR_LOST";
    break;
    case STATUS_WIN:
      statusText = "WIN";
    break;
    case STATUS_LOST:
      statusText = "LOST";
    break;
    case STATUS_OFF:
      statusText = "OFF";
    break;
    default:
      statusText = "STAND_BY";
    break;
  }


    Serial.println("STATUS :" + statusText);

}

// code stored in the sketch: Zoltar_init_2.ino
#include "Arduino.h"
#include "DFRobotDFPlayerMini.h"

DFRobotDFPlayerMini myDFPlayer;


const int STATUS_STAND_BY = -1;
const int STATUS_INIT = 0;
const int STATUS_ACTIVATE_GAME = 1;
const int STATUS_WAITING_RELEASE_COIN = 2;
const int STATUS_WIN_OR_LOST = 3;
const int STATUS_WIN = 4;
const int STATUS_LOST = 5;
const int STATUS_OFF = 6;

const int INIT_BUTTON_PIN = 7;

int status;

void setup() {
		status = STATUS_STAND_BY;
		pinMode(INIT_BUTTON_PIN, INPUT);
} 

void loop() {


	switch (status) {

    case STATUS_INIT:
			// Encender luces de fondo
			// Encender ojos
			// Encender movimiento de boca
			initMusic();
			delay(5000);
			// cambiamos al siguiente estado ACTIVATE_GAME
      break;

    case STATUS_ACTIVATE_GAME:
			// Encender luces "Apunta a la boca"
			// Encender sonido campana
			// Activar los mandos
			delay(10000);

			// Desactivar los mandos
			// Encender luces "Pulsa botón liberar moneda"
			// Activo siguiente estado WAITING_RELEASE_COIN

      break;

    case STATUS_WAITING_RELEASE_COIN:
			// Esperamos 10 segundos comprobando si se ha pulsado el botón de "liberar moneda"
			// Cuando se ha pulsado el botón o hayan pasado los 10 segundos, se libera la moneda.
			// Activo siguiente estado WIN_OR_LOST
      break;

		case STATUS_WIN_OR_LOST:
			// Chequeamos los sensores de acierto o no
			// Si ha acertado pasamos a "WIN" sino a "LOST"
      break;

		case STATUS_WIN:
				// Sacar tarjeta Acierto
				// Activar siguiente estado OFF
      break;

		case STATUS_LOST:
				// Sacar tarjeta de la tienda
				// Activar siguiente estado OFF
      break;

		case STATUS_OFF:
				// Esperar a que termine la música
				// desactivar musica y luces y movimiento. Todo
				// Activar siguiente estado STAND_BY
			break;

    default: //case "STAND_BY":
			standBy();
      break;

  }
}

void standBy() {

	// Esperando a que llegue la señal de la moneda
	// Y cambio al siguiente estado INIT

	int inputButton = digitalRead(INIT_BUTTON_PIN);
	Serial.println(inputButton);



}

void initMusic() {
	Serial.begin(9600);
  
  if (!myDFPlayer.begin(Serial)) {  //Use softwareSerial to communicate with mp3.
    while(true);
  }
  
  myDFPlayer.volume(30);  //Set volume value. From 0 to 30
  myDFPlayer.play(1);  //Play the first mp3
}
